// Logisim project IT012_Lab01_25520019.circ as structural Verilog: 6 circuits, main circuit Warmup
module Warmup (
  input  A,
  input  B,
  output F
);

  wire not_1_out;

  not not_1 (not_1_out, B);
  and and_1 (F, A, not_1_out);
endmodule

module TN1 (
  input  A,
  input  A_2,
  input  B,
  input  C,
  input  A_3,
  input  B_2,
  input  in_7,
  input  A_4,
  input  in_9,
  input  in_10,
  input  B_3,
  input  A_5,
  input  A_6,
  input  B_4,
  input  B_5,
  input  C_2,
  input  A_7,
  input  B_6,
  input  A_8,
  input  B_7,
  input  A_9,
  input  B_8,
  output F,
  output XOR3,
  output F_2,
  output NAND3,
  output F_3,
  output F_4,
  output CHAIN,
  output F_5,
  output F_6,
  output F_7
);

  wire NAND_3_out;

  not NOT (F, A);
  and AND (F_2, A_3, B_2);
  or OR (F_3, A_4, B_3);
  nand NAND (F_4, A_5, B_4);
  nor NOR (F_5, A_7, B_6);
  xor XOR (F_6, A_8, B_7);
  xnor XNOR (F_7, A_9, B_8);
  ExactlyOne xor_2 (.out(XOR3), .in0(A_2), .in1(B), .in2(C));
  nand nand_2 (NAND3, in_7, in_9, in_10);
  nand NAND_3 (NAND_3_out, A_6, B_5);
  nand nand_4 (CHAIN, NAND_3_out, C_2);
endmodule

module TN2 (
  input  x,
  input  y,
  input  z,
  output EQ1,
  output EQ2,
  output EQ3,
  output EQ4,
  output EQ5
);

  wire and_1_out, not_1_out, not_2_out, x___x_prime_y_out, x___y__prime_out, x___y_out, x___y_z_out,
       x___z_out, x_prime_y_out, x_prime_y_prime_out, x_y__prime_out, y_z_out;

  not not_1 (not_1_out, x);
  not not_2 (not_2_out, y);
  and x_prime_y_prime (x_prime_y_prime_out, not_1_out, not_2_out);
  nor x___y__prime (x___y__prime_out, y, x);
  nand x_y__prime (x_y__prime_out, x, y);
  or x___y (x___y_out, x, y);
  and y_z (y_z_out, y, z);
  and x_prime_y (x_prime_y_out, not_1_out, y);
  or x___z (x___z_out, z, x);
  or x___y_z (x___y_z_out, x, y_z_out);
  or x___x_prime_y (x___x_prime_y_out, x_prime_y_out, x);
  and and_1 (and_1_out, x___y_out, x___z_out);
  xnor xnor_1 (EQ1, x_prime_y_prime_out, x___y__prime_out);
  xnor xnor_2 (EQ2, x_prime_y_prime_out, x_y__prime_out);
  xnor xnor_3 (EQ3, and_1_out, x___y_z_out);
  xnor xnor_4 (EQ4, x___x_prime_y_out, x);
  xnor xnor_5 (EQ5, x___y_out, x___x_prime_y_out);
endmodule

module TN3 (
  input  A,
  input  B,
  input  C,
  input  D,
  output F
);

  wire and_1_out, and_2_out, and_3_out, and_4_out, and_5_out, and_6_out, not_1_out, not_2_out, not_3_out,
       not_4_out;

  not not_1 (not_1_out, A);
  not not_2 (not_2_out, B);
  not not_3 (not_3_out, C);
  not not_4 (not_4_out, D);
  and and_1 (and_1_out, not_1_out, not_2_out, C, not_4_out);
  and and_2 (and_2_out, not_1_out, not_2_out, C, D);
  and and_3 (and_3_out, not_1_out, B, not_3_out, D);
  and and_4 (and_4_out, not_1_out, B, C, D);
  and and_5 (and_5_out, A, not_2_out, C, D);
  and and_6 (and_6_out, A, B, not_3_out, D);
  or or_1 (F, and_1_out, and_2_out, and_3_out, and_4_out, and_5_out, and_6_out);
endmodule

module TN4 (
  input  A,
  input  B,
  input  C,
  input  D,
  output F_can,
  output EQ1,
  output F_sop,
  output EQ2,
  output F_pos
);

  wire and_1_out, and_2_out, and_3_out, and_4_out, and_5_out, and_6_out, and_7_out, and_8_out, and_9_out,
       not_1_out, not_2_out, not_3_out, not_4_out, or_1_out, or_2_out, or_3_out, or_4_out;

  not not_1 (not_1_out, A);
  not not_2 (not_2_out, B);
  not not_3 (not_3_out, C);
  not not_4 (not_4_out, D);
  and and_1 (and_1_out, not_1_out, not_2_out, C, not_4_out);
  and and_2 (and_2_out, not_1_out, not_2_out, C, D);
  and and_3 (and_3_out, not_1_out, B, not_3_out, D);
  and and_4 (and_4_out, not_1_out, B, C, D);
  and and_5 (and_5_out, A, not_2_out, C, D);
  and and_6 (and_6_out, A, B, not_3_out, D);
  and and_7 (and_7_out, not_1_out, not_2_out, C);
  and and_8 (and_8_out, not_1_out, B, D);
  and and_9 (and_9_out, B, not_3_out, D);
  or or_1 (or_1_out, B, C);
  or or_2 (or_2_out, not_2_out, D);
  or or_3 (or_3_out, not_1_out, D);
  or or_4 (or_4_out, not_1_out, not_2_out, not_3_out);
  or or_5 (F_can, and_1_out, and_2_out, and_3_out, and_4_out, and_5_out, and_6_out);
  or or_6 (F_sop, and_5_out, and_7_out, and_8_out, and_9_out);
  and and_10 (F_pos, or_1_out, or_2_out, or_3_out, or_4_out);
  xnor xnor_1 (EQ1, F_can, F_sop);
  xnor xnor_2 (EQ2, F_can, F_pos);
endmodule

module TN5 (
  input  A,
  input  B,
  input  C,
  output F
);

  wire xor_1_out;

  xor xor_1 (xor_1_out, A, B);
  xor xor_2 (F, xor_1_out, C);
endmodule
